// Logisim project OneBit.circ as structural Verilog: 6 circuits, main circuit main
module main (
  input  W,
  input  R,
  input  in_3,
  input  W_2,
  input  R_2,
  input  Address,
  input  W_3,
  input  R_3,
  input  W_4,
  input  R_4
);

  wire Bus_memory, Bus_write_data, or_1_out, Ram_cell_0, Ram_cell_1, Ram_write_data, X_memory, X_write_data,
       Y_memory, Y_write_data;

  // Probe on Ram_cell_0
  Ram Ram (
    .Read(R), .Read_Data(or_1_out), .Write(W), .Write_Data(Ram_write_data), .Address(Address),
    .Cell_0(Ram_cell_0), .Cell_1(Ram_cell_1));
  // Probe on Ram_cell_1
  or or_1 (or_1_out, Ram_write_data, in_3, Bus_write_data, Y_write_data, X_write_data);
  // Probe on X_memory
  Register X (.Read(R_2), .Read_Data(or_1_out), .Write(W_2), .Write_Data(X_write_data), .Memory(X_memory));
  Register Y (.Read(R_3), .Read_Data(or_1_out), .Write(W_3), .Write_Data(Y_write_data), .Memory(Y_memory));
  // Probe on Y_memory
  Register Bus (.Read(R_4), .Read_Data(or_1_out), .Write(W_4), .Write_Data(Bus_write_data), .Memory(Bus_memory));
  // Probe on Bus_memory

  // Notes on the sheet:
  //   Data Bus
endmodule

module Register (
  input  Read,
  input  Read_Data,
  input  Write,
  output Memory,
  output Write_Data
);

  wire nand_1_out, nand_2_out, nand_3_out, nand_4_out, nand_5_out, not_2_out;

  nand nand_1 (nand_1_out, Read, Read_Data);
  not not_1 (Write_Data, nand_2_out);
  nand nand_2 (nand_2_out, Memory, Write);
  not not_2 (not_2_out, nand_1_out);
  nand nand_3 (nand_3_out, nand_1_out, Read);
  nand nand_4 (nand_4_out, Read, not_2_out);
  nand nand_5 (nand_5_out, nand_3_out, Memory);
  nand nand_6 (Memory, nand_5_out, nand_4_out);
endmodule

module T_Trigger (
  input  Read
);

  wire nand_1_out, nand_2_out, nand_3_out, nand_4_out, nand_5_out, nand_6_out, nand_7_out, nand_8_out,
       not_1_out;

  not not_1 (not_1_out, Read);
  nand nand_1 (nand_1_out, nand_8_out, Read);
  nand nand_2 (nand_2_out, Read, nand_7_out);
  nand nand_3 (nand_3_out, nand_1_out, nand_4_out);
  nand nand_4 (nand_4_out, nand_3_out, nand_2_out);
  nand nand_5 (nand_5_out, nand_3_out, not_1_out);
  nand nand_6 (nand_6_out, not_1_out, nand_4_out);
  nand nand_7 (nand_7_out, nand_5_out, nand_8_out);
  nand nand_8 (nand_8_out, nand_7_out, nand_6_out);
endmodule

module T_Trigger2 (
  input  in_1
);

  wire nand_1_out, nand_2_out, nand_3_out, nand_4_out, nand_5_out, nand_6_out;

  nand nand_1 (nand_1_out, in_1, nand_2_out);
  nand nand_2 (nand_2_out, nand_1_out, nand_4_out);
  nand nand_3 (nand_3_out, nand_1_out, in_1, nand_4_out);
  nand nand_4 (nand_4_out, nand_3_out, nand_6_out);
  nand nand_5 (nand_5_out, nand_1_out, nand_6_out);
  nand nand_6 (nand_6_out, nand_5_out, nand_3_out);
endmodule

module Ram (
  input  Read,
  input  Read_Data,
  input  Write,
  input  Address,
  output Cell_0,
  output Cell_1,
  output Write_Data
);

  wire Cell_0_write_data, Cell_1_write_data, nor_1_out, nor_2_out, nor_3_out, nor_4_out, not_1_out,
       not_2_out, not_3_out;

  or or_1 (Write_Data, Cell_0_write_data, Cell_1_write_data);
  not not_1 (not_1_out, Write);
  nor nor_1 (nor_1_out, not_2_out, not_1_out);
  nor nor_2 (nor_2_out, not_1_out, Address);
  Register u_Cell_0 (
    .Read(nor_4_out), .Read_Data(Read_Data), .Write(nor_2_out), .Write_Data(Cell_0_write_data),
    .Memory(Cell_0));
  Register u_Cell_1 (
    .Read(nor_3_out), .Read_Data(Read_Data), .Write(nor_1_out), .Write_Data(Cell_1_write_data),
    .Memory(Cell_1));
  not not_2 (not_2_out, Address);
  not not_3 (not_3_out, Read);
  nor nor_3 (nor_3_out, not_2_out, not_3_out);
  nor nor_4 (nor_4_out, not_3_out, Address);
endmodule

module Decoder_3_8 (
  input  _0,
  input  _1,
  input  _2,
  output _0_2,
  output _1_2,
  output _2_2,
  output _3,
  output _4,
  output _5,
  output _6,
  output _7
);

  wire not_1_out, not_2_out, not_3_out;

  not not_1 (not_1_out, _0);
  not not_2 (not_2_out, _1);
  not not_3 (not_3_out, _2);
  and and_1 (_0_2, not_1_out, not_2_out, not_3_out);
  and and_2 (_1_2, _0, not_2_out, not_3_out);
  and and_3 (_2_2, not_1_out, not_3_out, _1);
  and and_4 (_3, not_3_out, _0, _1);
  and and_5 (_4, not_1_out, not_2_out, _2);
  and and_6 (_5, not_2_out, _0, _2);
  and and_7 (_6, not_1_out, _1, _2);
  and and_8 (_7, _0, _1, _2);
endmodule
